# Fritzing sketch Parking Sensor( for NANO) (saved by Fritzing 0.9.3b)
circuit board: 8.46667cm x 5.64444cm
breadboards: 1

parts:
  LCD1 = LCD screen
  J1 = Piezo Speaker
  hc-sr1 = hc-sr04
  hc-sr2 = hc-sr04
  R1 = Rotary Potentiometer (Small) [maximum_resistance=100kΩ package=THT]
  R2 = Resistor [tolerance=±5% resistance=220 package=THT]
  Part2 = Arduino Nano (Rev3.0) (ICSP)

nets:
  GND: LCD1.VSS, LCD1.R/W, LCD1.LED-, J1.pin1, hc-sr1.GND, hc-sr2.GND, R1.leg1, Part2.GND
  VCC: LCD1.VDD, hc-sr1.VCC, hc-sr2.VCC, R1.leg2, R2.Pin_1, Part2.5V
  N1: LCD1.V0, R1.wiper
  N2: LCD1.RS, Part2.D1/TX
  N3: LCD1.E, Part2.D2
  N4: LCD1.DB4, Part2.D4
  N5: LCD1.DB5, Part2.D5
  N6: LCD1.DB6, Part2.D6
  N7: LCD1.DB7, Part2.D7
  N8: LCD1.LED+, R2.Pin_0
  N9: J1.pin2, Part2.D13/SCK
  N10: hc-sr1.Trig, Part2.A2
  N11: hc-sr1.Echo, Part2.A3
  N12: hc-sr2.Trig, Part2.A0
  N13: hc-sr2.Echo, Part2.A1

// code stored in the sketch: two ultrasonic one lcd.ino

