# Fritzing sketch Parking Sensor (saved by Fritzing 0.9.3b)
circuit board: 8.46667cm x 5.64444cm
breadboards: 1

parts:
  Part1 = Arduino Uno (Rev3)
  LCD1 = LCD screen
  J1 = Piezo Speaker
  hc-sr1 = hc-sr04
  hc-sr2 = hc-sr04
  R1 = Rotary Potentiometer (Small) [maximum_resistance=100kΩ package=THT]
  R2 = Resistor [tolerance=±5% resistance=220 package=THT]

nets:
  N1: Part1.A0, hc-sr2.Trig
  N2: Part1.A1, hc-sr2.Echo
  N3: Part1.A2, hc-sr1.Trig
  N4: Part1.A3, hc-sr1.Echo
  N5: Part1.D13/SCK, J1.pin2
  GND: Part1.GND, LCD1.VSS, LCD1.R/W, LCD1.LED-, J1.pin1, hc-sr1.GND, hc-sr2.GND, R1.leg1
  N6: Part1.D1/TX, LCD1.RS
  N7: Part1.D2, LCD1.E
  N8: Part1.D4, LCD1.DB4
  N9: Part1.D5_PWM, LCD1.DB5
  N10: Part1.D6_PWM, LCD1.DB6
  N11: Part1.D7, LCD1.DB7
  VCC: Part1.5V, LCD1.VDD, hc-sr1.VCC, hc-sr2.VCC, R1.leg2, R2.Pin_1
  N12: LCD1.V0, R1.wiper
  N13: LCD1.LED+, R2.Pin_0

// code stored in the sketch: two ultrasonic one lcd.ino

